# Fritzing sketch Arcade-button-prototype-v1 (saved by Fritzing 0.9.1b)
circuit board: 6.19794cm x 2.70966cm
breadboards: 1

parts:
  Spark_Core = Spark Core (v1.0)
  #3 = Header 2 [package=jst-2-pth]
  #5 = Header 2 [package=jst-2-pth]
  #1 = Header 2 [package=jst-2-pth]
  #4 = Header 2 [package=jst-2-pth]
  #2 = Header 2 [package=jst-2-pth]
  #6 = Header 2 [package=jst-2-pth]
  Neopixel = mystery part, 3 pins [chip_label=?]

nets:
  N1: Spark_Core.GND, #3.1, #5.1, #1.1, #4.1, #2.1, #6.1, Neopixel.pin2
  N2: Spark_Core.D0, #1.2
  N3: Spark_Core.D1, #2.2
  N4: Spark_Core.D2, #3.2
  N5: Spark_Core.D3, #4.2
  N6: Spark_Core.D4, #5.2
  N7: Spark_Core.D5, #6.2
  N8: Spark_Core.D6, Neopixel.pin1
  N9: Spark_Core.3V3, Neopixel.pin3
